# Fritzing sketch lizard-enclosure-wiring-diagram (saved by Fritzing 0.9.3b)

parts:
  RaspberryPi1 = Raspberry Pi Model B
  CAPSENSE1 = AT42QT1010 Momentary Capsense Breakout
  CAMERA1 = TTL Serial JPEG Camera  # not connected
  Grove1 = Grove Buzz
  Grove2 = Grove Buzz

nets:
  VCC: RaspberryPi1.5V, CAPSENSE1.VDD, Grove1.VCC, Grove2.VCC
  GND: RaspberryPi1.SCL, CAPSENSE1.GND, Grove1.GND, Grove2.GND
  N1: RaspberryPi1.#18, Grove2.SIG
  N2: RaspberryPi1.#23, Grove1.SIG
  N3: RaspberryPi1.#25, CAPSENSE1.OUT

notes:
  This is a Grove Relay connected to the UV lights (couldnt' find the part).
  This is a Grove Relay connected to the Humidifier (couldnt' find the part).

custom parts:
  Raspberry Pi Model B: Raspberry Pi (Model B)
  AT42QT1010 Momentary Capsense Breakout: A capacitive touch momentary switch breakout for the AT42QT1010 chip.
  TTL Serial JPEG Camera: TTL Serial JPEG Camera with NTSC Out
