# Fritzing sketch lizard-enclosure-wiring-diagram (saved by Fritzing 0.8.3b)

parts:
  RaspberryPi1 = Raspberry Pi Model B
  CAPSENSE1 = AT42QT1010 Momentary Capsense Breakout
  CAMERA1 = TTL Serial JPEG Camera  # not connected

nets:
  5V: RaspberryPi1.5V, CAPSENSE1.VDD
  N1: RaspberryPi1.SCL, CAPSENSE1.GND
  N2: RaspberryPi1.#25, CAPSENSE1.OUT

custom parts:
  Raspberry Pi Model B: Raspberry Pi (Model B)
  AT42QT1010 Momentary Capsense Breakout: A capacitive touch momentary switch breakout for the AT42QT1010 chip.
  TTL Serial JPEG Camera: TTL Serial JPEG Camera with NTSC Out
